// Digital circuit CPU.dig as structural Verilog
module CPU (
  output [15:0] out_1,
  output [3:0] out_2,
  output [1:0] out_3,
  output [1:0] out_4,
  output [1:0] out_5,
  output [7:0] out_6,
  output [3:0] out_7,
  output [15:0] out_8,
  output [15:0] out_9,
  output [15:0] out_10,
  output [15:0] out_11,
  output [15:0] out_12
);

  wire button_1_out, control_unit_1_p2, control_unit_1_p3;
  wire [1:0] multiplexer_1_out;
  wire [15:0] bitextender_1_out, multiplexer_2_out, register_file_1_reg_1_value, register_file_1_reg_2_value;

  Button button_1 (.out(button_1_out));
  Program_Counter program_counter_1 (.address_i(4'b0000), .write(1'b0), .CLK(button_1_out), .address_o(out_7));
  Program_Memory program_memory_1 (.address(out_7), .instruction(out_8));
  Decoder decoder_1 (
    .instruction(out_8), .opcode(out_2), .rs(out_3), .rt(out_4), .immediate({out_6[7:2], out_5}));  // open: address
  // Control_Unit control_unit_1: pin names not known; wires that end beside it: out_2, control_unit_1_p2, control_unit_1_p3
  Multiplexer #(.Bits(2)) multiplexer_1 (.sel(control_unit_1_p2), .in_0(out_4), .in_1(out_5), .out(multiplexer_1_out));
  BitExtender bitextender_1 (.in({out_6[7:2], out_5}), .out(bitextender_1_out));
  Register_File register_file_1 (
    .Reg_1_Read(out_3), .Reg_2_Read(out_4), .Reg_Write(multiplexer_1_out), .data(out_1), .CLK(button_1_out),
    .Reg_1_Value(register_file_1_reg_1_value), .Reg_2_Value(register_file_1_reg_2_value), .R1(out_9),
    .R2(out_10), .R3(out_11), .R4(out_12));
  Multiplexer #(.Bits(16)) multiplexer_2 (
    .sel(control_unit_1_p3), .in_0(register_file_1_reg_2_value), .in_1(bitextender_1_out),
    .out(multiplexer_2_out));
  ALU alu_1 (.Left(register_file_1_reg_1_value), .Right(multiplexer_2_out), .result(out_1));

  assign out_6[1:0] = out_5;

  // Other names for the same wires on the sheet: imm[7:0] = {out_6[7:2], out_5}; rd[1:0] = out_5;
  //   instruction[15:0] = out_8; opcode[3:0] = out_2; pc[3:0] = out_7; R1[15:0] = out_9; R2[15:0] = out_10;
  //   R3[15:0] = out_11; R4[15:0] = out_12; rs[1:0] = out_3; rt[1:0] = out_4
endmodule
